// Logisim project mips-like_monociclico.circ as structural Verilog: 5 circuits, main circuit PROCESSADOR
module PROCESSADOR (
  output [31:0] \INSTRUÇÃO ,
  output [31:0] \INSTRUÇÃO_2 
);

  wire and_1_out, Bge, Branch, button_1_out, clock_1_out, j, or_1_out, UC_mem_read, UC_mem_write, UC_op0,
       UC_op1, UC_op2, UC_write_reg, ULASrc;
  wire [7:0] PC_q_2;
  wire [31:0] adder_1_out, banco_de_registradores_1_r0_d, banco_de_registradores_1_r1_d, bit_extender_1_out,
       bit_extender_2_out, \memória_de_dados_1_saída , multiplexer_1_out, multiplexer_2_out,
       multiplexer_3_out, PC_q, ula_1_ula_out;

  and and_1 (and_1_out, Branch, Bge);
  Adder #(.width(32)) adder_1 (.a({PC_q[31:10], PC_q_2, PC_q[1:0]}), .b(32'h4), .out(adder_1_out));  // open: cin, cout
  Multiplexer #(.width(32), .enable("false")) multiplexer_1 (
    .in0(adder_1_out), .in1(bit_extender_1_out), .out(multiplexer_1_out), .sel(or_1_out));
  assign bit_extender_1_out = {{16{1'b0}}, \INSTRUÇÃO [15:0]};  // Bit_Extender bit_extender_1
  or or_1 (or_1_out, and_1_out, j);
  Register #(.width(32)) PC (
    .D(multiplexer_1_out), .Q({PC_q[31:10], PC_q_2, PC_q[1:0]}), .clk(clock_1_out), .clr(button_1_out));  // open: en
  Button button_1 (.out(button_1_out));
  Clock clock_1 (.out(clock_1_out));
  ROM #(.dataWidth(32)) rom_1 (.addr(PC_q_2), .data(\INSTRUÇÃO ));  // open: sel
  UC UC (
    .E3(\INSTRUÇÃO [31]), .E2(\INSTRUÇÃO [30]), .E1(\INSTRUÇÃO [29]), .E0(\INSTRUÇÃO [28]), .OP0(UC_op0),
    .OP1(UC_op1), .OP2(UC_op2), .write_reg(UC_write_reg), .mem_write(UC_mem_write), .mem_read(UC_mem_read),
    .j(j), .ULASrc(ULASrc), .Branch(Branch));
  BANCO_DE_REGISTRADORES banco_de_registradores_1 (
    .DATA_WRITE(multiplexer_3_out), .CLK(clock_1_out), .RW(\INSTRUÇÃO [27:24]),
    .R0_D(banco_de_registradores_1_r0_d), .R1_D(banco_de_registradores_1_r1_d), .R1(\INSTRUÇÃO [23:20]),
    .RW_2(UC_write_reg), .RESET(button_1_out), .R0(\INSTRUÇÃO [19:16]));
  Multiplexer #(.width(32), .enable("false")) multiplexer_2 (
    .in0(banco_de_registradores_1_r1_d), .in1(bit_extender_2_out), .out(multiplexer_2_out), .sel(ULASrc));
  assign bit_extender_2_out = {{16{1'b0}}, \INSTRUÇÃO [15:0]};  // Bit_Extender bit_extender_2
  ULA ula_1 (
    .DATA_0(banco_de_registradores_1_r0_d), .DATA_1(multiplexer_2_out), .ULA_OUT(ula_1_ula_out),
    .ULA_OP0(UC_op0), .ULA_OP1(UC_op1), .Deslocamento({1'b0, \INSTRUÇÃO [15:12]}), .ULA_OP2(UC_op2), .bge(Bge));
  Multiplexer #(.width(32), .enable("false")) multiplexer_3 (
    .in0(ula_1_ula_out), .in1(\memória_de_dados_1_saída ), .out(multiplexer_3_out), .sel(UC_mem_read));
  \MEMÓRIA_DE_DADOS  \memória_de_dados_1  (
    .\Endereço (banco_de_registradores_1_r0_d), .Valor(multiplexer_2_out),
    .\Saída (\memória_de_dados_1_saída ), .MemWrite(UC_mem_write), .CLK(clock_1_out), .MemRead(UC_mem_read));

  // Other names for the same wires on the sheet: End_Imm[15:0] = \INSTRUÇÃO [15:0]

  // Notes on the sheet:
  //   REG_0
  //   REG_1
  //   REG_W
  //   contents of rom_1 (hex, n*v repeats v):
  //   1120000 3000
  //   DATA_W
  //   BANCO DE REGISTRADORES
  //   REG0_D
  //   REG1_D
  //   ULA
endmodule

module ULA (
  input  [4:0] Deslocamento,
  input  [31:0] DATA_0,
  input  [31:0] DATA_1,
  input  ULA_OP0,
  input  ULA_OP1,
  input  ULA_OP2,
  output [31:0] ULA_OUT,
  output bge
);

  wire comparator_1_lt;
  wire [31:0] adder_1_out, multiplier_1_out, negator_1_out, or_1_out, shifter_1_out, subtractor_1_out;

  Adder #(.width(32)) adder_1 (.a(DATA_0), .b(DATA_1), .out(adder_1_out));  // open: cin, cout
  Subtractor #(.width(32)) subtractor_1 (.a(DATA_0), .b(DATA_1), .out(subtractor_1_out));  // open: bin, bout
  Multiplier #(.width(32)) multiplier_1 (.a(DATA_0), .b(DATA_1), .out(multiplier_1_out));  // open: cin, cout
  Shifter #(.width(32)) shifter_1 (.in(DATA_0), .\dist (Deslocamento), .out(shifter_1_out));
  assign or_1_out = DATA_0 | DATA_1;  // OR_Gate or_1, 32 bits wide
  Negator #(.width(32)) negator_1 (.in(DATA_0), .out(negator_1_out));
  Comparator #(.width(32), .mode("unsigned")) comparator_1 (
    .a(DATA_0), .b(DATA_1), .lt(comparator_1_lt));  // open: gt, eq
  not not_1 (bge, comparator_1_lt);
  Multiplexer #(.select(3), .width(32), .enable("false")) multiplexer_1 (
    .in0(adder_1_out), .in1(subtractor_1_out), .in2(multiplier_1_out), .in3(shifter_1_out), .in4(or_1_out),
    .in5(negator_1_out), .out(ULA_OUT), .sel({ULA_OP0, ULA_OP1, ULA_OP2}));  // open: in6, in7
endmodule

module UC (
  input  E3,
  input  E2,
  input  E1,
  input  E0,
  output OP0,
  output OP1,
  output OP2,
  output write_reg,
  output mem_write,
  output mem_read,
  output j,
  output ULASrc,
  output Branch
);

  wire and_3_out, and_4_out, and_5_out, and_6_out, and_7_out, and_8_out, and_12_out, and_13_out, not_1_out,
       not_2_out, not_3_out, not_4_out, not_5_out, not_6_out, not_7_out, not_8_out, not_9_out, not_10_out,
       not_11_out, not_12_out, not_13_out, not_14_out, not_15_out, not_16_out, not_17_out, not_18_out;

  and and_1 (OP0, E2, not_1_out);
  not not_1 (not_1_out, E1);
  not not_2 (not_2_out, E3);
  not not_3 (not_3_out, E2);
  and and_2 (OP1, not_2_out, not_3_out, E1);
  not not_4 (not_4_out, E3);
  not not_5 (not_5_out, E2);
  and and_3 (and_3_out, not_4_out, not_5_out, E0);
  not not_6 (not_6_out, E3);
  and and_4 (and_4_out, not_6_out, not_7_out, E0);
  not not_7 (not_7_out, E1);
  not not_8 (not_8_out, E3);
  and and_5 (and_5_out, not_8_out, not_9_out);
  not not_9 (not_9_out, E2);
  not not_10 (not_10_out, E3);
  and and_6 (and_6_out, not_10_out, not_11_out);
  not not_11 (not_11_out, E1);
  not not_12 (not_12_out, E1);
  and and_7 (and_7_out, not_12_out, E0);
  and and_8 (and_8_out, E1, not_13_out);
  not not_13 (not_13_out, E0);
  and and_9 (mem_write, E2, E1, E0);
  and and_10 (mem_read, E2, E1, not_14_out);
  not not_14 (not_14_out, E0);
  not not_15 (not_15_out, E1);
  and and_11 (j, E3, not_15_out, not_16_out);
  not not_16 (not_16_out, E0);
  not not_17 (not_17_out, E1);
  and and_12 (and_12_out, E3, not_17_out, E0);
  and and_13 (and_13_out, E3, E1, not_18_out);
  not not_18 (not_18_out, E0);
  and and_14 (Branch, E3, E1, E0);
  or or_1 (OP2, and_3_out, and_4_out);
  or or_2 (write_reg, and_5_out, and_6_out, and_7_out, and_8_out);
  or or_3 (ULASrc, and_12_out, and_13_out);
endmodule

module BANCO_DE_REGISTRADORES (
  input  [31:0] DATA_WRITE,
  input  [3:0] R0,
  input  [3:0] R1,
  input  CLK,
  input  [3:0] RW,
  input  RESET,
  input  RW_2,
  output [31:0] R0_D,
  output [31:0] R1_D
);

  wire demultiplexer_1_out0, demultiplexer_1_out1, demultiplexer_1_out2, demultiplexer_1_out3,
       demultiplexer_1_out4, demultiplexer_1_out5, demultiplexer_1_out6, demultiplexer_1_out7,
       demultiplexer_1_out8, demultiplexer_1_out9, demultiplexer_1_out10, demultiplexer_1_out11,
       demultiplexer_1_out12, demultiplexer_1_out13, demultiplexer_1_out14, demultiplexer_1_out15;
  wire [31:0] register_1_q, register_2_q, register_3_q, register_4_q, register_5_q, register_6_q,
       register_7_q, register_8_q, register_9_q, register_10_q, register_11_q, register_12_q, register_13_q,
       register_14_q, register_15_q, register_16_q;

  Register #(.width(32)) register_1 (.D(DATA_WRITE), .Q(register_1_q), .clr(demultiplexer_1_out0));  // open: en, clk
  Demultiplexer #(.select(4), .enable("false")) demultiplexer_1 (
    .out0(demultiplexer_1_out0), .out1(demultiplexer_1_out1), .out2(demultiplexer_1_out2),
    .out3(demultiplexer_1_out3), .out4(demultiplexer_1_out4), .out5(demultiplexer_1_out5),
    .out6(demultiplexer_1_out6), .out7(demultiplexer_1_out7), .out8(demultiplexer_1_out8),
    .out9(demultiplexer_1_out9), .out10(demultiplexer_1_out10), .out11(demultiplexer_1_out11),
    .out12(demultiplexer_1_out12), .out13(demultiplexer_1_out13), .out14(demultiplexer_1_out14),
    .out15(demultiplexer_1_out15), .in(RW_2), .sel(RW));
  Register #(.width(32)) register_2 (
    .D(DATA_WRITE), .en(demultiplexer_1_out1), .Q(register_2_q), .clk(CLK), .clr(RESET));
  Register #(.width(32)) register_3 (
    .D(DATA_WRITE), .en(demultiplexer_1_out2), .Q(register_3_q), .clk(CLK), .clr(RESET));
  Register #(.width(32)) register_4 (
    .D(DATA_WRITE), .en(demultiplexer_1_out3), .Q(register_4_q), .clk(CLK), .clr(RESET));
  Register #(.width(32)) register_5 (
    .D(DATA_WRITE), .en(demultiplexer_1_out4), .Q(register_5_q), .clk(CLK), .clr(RESET));
  Register #(.width(32)) register_6 (
    .D(DATA_WRITE), .en(demultiplexer_1_out5), .Q(register_6_q), .clk(CLK), .clr(RESET));
  Register #(.width(32)) register_7 (
    .D(DATA_WRITE), .en(demultiplexer_1_out6), .Q(register_7_q), .clk(CLK), .clr(RESET));
  Register #(.width(32)) register_8 (
    .D(DATA_WRITE), .en(demultiplexer_1_out7), .Q(register_8_q), .clk(CLK), .clr(RESET));
  Register #(.width(32)) register_9 (
    .D(DATA_WRITE), .en(demultiplexer_1_out8), .Q(register_9_q), .clk(CLK), .clr(RESET));
  Register #(.width(32)) register_10 (
    .D(DATA_WRITE), .en(demultiplexer_1_out9), .Q(register_10_q), .clk(CLK), .clr(RESET));
  Register #(.width(32)) register_11 (
    .D(DATA_WRITE), .en(demultiplexer_1_out10), .Q(register_11_q), .clk(CLK), .clr(RESET));
  Register #(.width(32)) register_12 (
    .D(DATA_WRITE), .en(demultiplexer_1_out11), .Q(register_12_q), .clk(CLK), .clr(RESET));
  Register #(.width(32)) register_13 (
    .D(DATA_WRITE), .en(demultiplexer_1_out12), .Q(register_13_q), .clk(CLK), .clr(RESET));
  Register #(.width(32)) register_14 (
    .D(DATA_WRITE), .en(demultiplexer_1_out13), .Q(register_14_q), .clk(CLK), .clr(RESET));
  Register #(.width(32)) register_15 (
    .D(DATA_WRITE), .en(demultiplexer_1_out14), .Q(register_15_q), .clk(CLK), .clr(RESET));
  Register #(.width(32)) register_16 (
    .D(DATA_WRITE), .en(demultiplexer_1_out15), .Q(register_16_q), .clk(CLK), .clr(RESET));
  Multiplexer #(.select(4), .width(32), .disabled(0), .enable("false")) multiplexer_1 (
    .in0(register_1_q), .in1(register_2_q), .in2(register_3_q), .in3(register_4_q), .in4(register_5_q),
    .in5(register_6_q), .in6(register_7_q), .in7(register_8_q), .in8(register_9_q), .in9(register_10_q),
    .in10(register_11_q), .in11(register_12_q), .in12(register_13_q), .in13(register_14_q),
    .in14(register_15_q), .in15(register_16_q), .out(R0_D), .sel(R0));
  Multiplexer #(.select(4), .width(32), .enable("false")) multiplexer_2 (
    .in0(register_1_q), .in1(register_2_q), .in2(register_3_q), .in3(register_4_q), .in4(register_5_q),
    .in5(register_6_q), .in6(register_7_q), .in7(register_8_q), .in8(register_9_q), .in9(register_10_q),
    .in10(register_11_q), .in11(register_12_q), .in12(register_13_q), .in13(register_14_q),
    .in14(register_15_q), .in15(register_16_q), .out(R1_D), .sel(R1));
endmodule

// MD
module \MEMÓRIA_DE_DADOS  (
  input  [31:0] \Endereço ,
  input  MemRead,
  input  [31:0] Valor,
  input  MemWrite,
  input  CLK,
  output [31:0] \Saída 
);

  wire [31:0] ram_1_data;

  RAM #(.addrWidth(24), .dataWidth(32), .bus("separate")) ram_1 (
    .addr(\Endereço [23:0]), .din(Valor), .data(ram_1_data), .str(MemWrite), .clk(CLK));  // open: sel, ld, clr
  Multiplexer #(.width(32), .enable("false")) multiplexer_1 (
    .in0(\Endereço ), .in1(ram_1_data), .out(\Saída ), .sel(MemRead));
endmodule
